// Logisim project cpu.circ as structural Verilog: 3 circuits, main circuit main
module main (
  input  [15:0] INSTRUCTION,
  input  CLOCK,
  output [15:0] FETCH_ADDRESS,
  output [15:0] L_s0_Value_555821f6,
  output [15:0] L_s1_Value_bb868b5b,
  output [15:0] L_s2_Value_1029e135,
  output [15:0] L_ra_Value_3ae5280b,
  output [15:0] L_sp_Value_256d6ed0,
  output [15:0] L_HI_Value_4d3aacc1,
  output [15:0] L_LO_Value_6d74149f
);

  wire [2:0] instruction_decoder_1_rd, instruction_decoder_1_rs, instruction_decoder_1_rt, multiplexer_1_out;
  wire [15:0] adder_4_1_pc_out;

  Register #(.width(16)) L_PC_1fb09d07 (.D(adder_4_1_pc_out), .en(1'b1), .clk(CLOCK), .Q(FETCH_ADDRESS));  // open: clr
  Adder_4 adder_4_1 (.PC_out(adder_4_1_pc_out), .PC_in(FETCH_ADDRESS));
  Instruction_decoder instruction_decoder_1 (
    .rs(instruction_decoder_1_rs), .Instruction(INSTRUCTION), .rd(instruction_decoder_1_rd),
    .rt(instruction_decoder_1_rt));  // open: funct, immediate, opcode
  Multiplexer #(.width(3), .enable("false")) multiplexer_1 (
    .in0(instruction_decoder_1_rt), .in1(instruction_decoder_1_rd), .out(multiplexer_1_out));  // open: sel
  regfile_main main_1 (
    .Read_Register_1_a0c8cd62(instruction_decoder_1_rs), .Read_Register_2_6a35ea3b(multiplexer_1_out),
    .Write_Register_a5712683(instruction_decoder_1_rd));  // open: Write_Data_73679b02, Write_Enable_cb4a62c6, Clock, Read_Data_1_d638ea5b, Read_Data_2_45f3f23e, L_s0_Value_319056dc, L_s1_Value_178742e2, L_s2_Value_c4d9ac04, L_ra_Value_229931e7, L_sp_Value_102b2bfe
  // alu_main main_2: pin names not known
  Register #(.width(16)) L_HI_108849eb ();  // open: D, en, Q, clk, clr
  Register #(.width(16)) L_LO_6db75bec ();  // open: D, en, Q, clk, clr
  // mem_main MEM: pin names not known

  // Other names for the same wires on the sheet: clk = CLOCK; fetch_addr[15:0] = FETCH_ADDRESS

  // Notes on the sheet:
  //   Output
  //   mudar adder
  //   These are outputs/inputs from run.circ
  //   Inputs
  //   These are DEBUG/TEST outputs from your circuit.
endmodule

module Adder_4 (
  input  [15:0] PC_in,
  output [15:0] PC_out
);

  Adder #(.width(16)) adder_1 (.a(PC_in), .b(16'h2), .out(PC_out));  // open: cin, cout
endmodule

module Instruction_decoder (
  input  [15:0] Instruction,
  output [2:0] funct,
  output [2:0] rt,
  output [2:0] rs,
  output [9:0] immediate,
  output [2:0] rd,
  output [3:0] opcode
);


  assign funct = Instruction[2:0];
  assign immediate = Instruction[9:0];
  assign opcode = Instruction[15:12];
  assign rd = Instruction[11:9];
  assign rs = Instruction[8:6];
  assign rt = Instruction[5:3];
endmodule
